// Logisim project BrianLinCPUhomework4.circ as structural Verilog: 15 circuits, main circuit singleRegister
module main (
  input  reset,
  input  [15:0] in_2,
  output [15:0] out_3,
  output [15:0] PC_1,
  output [15:0] Current_PC,
  output [3:0] out_6,
  output [15:0] out_7,
  output [15:0] out_8,
  output [15:0] out_9,
  output [2:0] out_10,
  output [11:0] out_11,
  output [2:0] out_12,
  output [2:0] out_13,
  output [2:0] out_14,
  output [15:0] out_15,
  output [3:0] out_16,
  output [15:0] out_17,
  output [15:0] out_18,
  output [15:0] out_19,
  output [15:0] out_20,
  output [15:0] out_21,
  output [15:0] out_22,
  output [15:0] out_23,
  output [15:0] out_24
);

  wire aluImm, and_1_out, beq, blt, branch, clock, \input , isBeq, j, jal, jr, keyboard_1_avail, memToReg,
       multiplexer_2_out, or_1_out, \output , regDest, we, writeMem;
  wire [2:0] multiplexer_1_out, multiplexer_3_out, multiplexer_4_out;
  wire [6:0] keyboard_1_data;
  wire [8:8] not_1_out;
  wire [15:0] branchAmount_sum, multiplexer_5_out, multiplexer_6_out, multiplexer_8_out, multiplexer_9_out,
       multiplexer_10_out, multiplexer_11_out, ram_1_data;

  Clock u_clock (.out(clock));
  PC PC (.Clock(clock), .In(out_3), .Reset(reset), .Out(Current_PC));
  ROM #(.addrWidth(16), .dataWidth(16)) rom_1 ();  // open: addr, data, sel
  _16bitAdder u_16bitadder_1 (.carryIn(1'b0), .InputA(16'h1), .InputB(Current_PC), .Sum(PC_1));  // open: carryOut
  _16bitAdder branchAmount (.carryIn(1'b0), .InputA(PC_1), .InputB(out_15), .Sum(branchAmount_sum));  // open: carryOut
  Instruction_Splitter instruction_splitter_1 (
    .instruction(in_2), .shAmt(out_10), .rd(out_12), .rt(out_13), .rs(out_14), .opcode(out_6),
    .address(out_11), .immed(out_15));
  Control control_1 (
    .opcode(out_6), .regDest(regDest), .aluImm(aluImm), .branch(branch), .memToReg(memToReg),
    .writeMem(writeMem), .j(j), .jal(jal), .jr(jr), .\input (\input ), .\output (\output ), .writingReg(we),
    .beq(isBeq));
  Multiplexer #(.width(3), .enable("false")) multiplexer_1 (
    .in0(out_13), .in1(out_12), .out(multiplexer_1_out), .sel(regDest));
  Multiplexer #(.enable("false")) multiplexer_2 (.in0(blt), .in1(beq), .out(multiplexer_2_out), .sel(isBeq));
  Multiplexer #(.width(3), .enable("false")) multiplexer_3 (
    .in0(multiplexer_1_out), .in1(3'b111), .out(multiplexer_3_out), .sel(jal));
  Multiplexer #(.width(3), .enable("false")) multiplexer_4 (
    .in0(out_14), .in1(out_12), .out(multiplexer_4_out), .sel(jr));
  Multiplexer #(.width(16), .enable("false")) multiplexer_5 (
    .in0(PC_1), .in1(branchAmount_sum), .out(multiplexer_5_out), .sel(and_1_out));
  and and_1 (and_1_out, branch, multiplexer_2_out);
  Multiplexer #(.width(16), .enable("false")) multiplexer_6 (
    .in0(multiplexer_5_out), .in1({Current_PC[15:12], out_11}), .out(multiplexer_6_out), .sel(or_1_out));
  or or_1 (or_1_out, j, jal);
  Multiplexer #(.width(16), .enable("false")) multiplexer_7 (
    .in0(multiplexer_6_out), .in1(out_8), .out(out_3), .sel(jr));
  registerFile registerfile_1 (
    .Reset(reset), .RegWriteEnable(we), .WriteReg(multiplexer_3_out), .ReadReg1(multiplexer_4_out),
    .ReadReg2(out_13), .WriteData(multiplexer_9_out), .ReadData1(out_8), .ReadData2(out_9), .reg0(out_17),
    .reg1(out_18), .reg2(out_19), .reg3(out_20), .reg4(out_21), .reg5(out_22), .reg6(out_23), .reg7(out_24),
    .Clock(clock));
  Multiplexer #(.width(16), .enable("false")) multiplexer_8 (
    .in0(out_9), .in1(out_15), .out(multiplexer_8_out), .sel(aluImm));
  Keyboard keyboard_1 (.clk(clock), .re(\input ), .clr(reset), .avail(keyboard_1_avail), .data(keyboard_1_data));
  TTY tty_1 (.data(out_8[6:0]), .clk(clock), .we(1'b1), .clr(reset));
  not not_1 (not_1_out[8], keyboard_1_avail);
  TTY tty_2 (.data(out_8[6:0]), .clk(clock), .we(\output ), .clr(reset));
  ALU alu_1 (
    .rs(out_8), .rt(multiplexer_8_out), .shiftAmount(out_10), .opcode(out_6), .OutputData(out_7),
    .beq_1001(beq), .blt_1010(blt));
  Multiplexer #(.width(16), .enable("false")) multiplexer_9 (
    .in0(multiplexer_10_out), .in1({{7{1'b0}}, not_1_out[8], 1'b0, keyboard_1_data}),
    .out(multiplexer_9_out), .sel(\input ));
  Multiplexer #(.width(16), .enable("false")) multiplexer_10 (
    .in0(multiplexer_11_out), .in1(PC_1), .out(multiplexer_10_out), .sel(jal));
  RAM #(.addrWidth(16), .dataWidth(16), .bus("separate")) ram_1 (
    .addr(out_7), .din(out_9), .data(ram_1_data), .str(writeMem), .clk(clock), .clr(reset));  // open: sel, ld
  Multiplexer #(.width(16), .enable("false")) multiplexer_11 (
    .in0(out_7), .in1(ram_1_data), .out(multiplexer_11_out), .sel(memToReg));

  assign out_16 = out_6;

  // Other names for the same wires on the sheet: addr[11:0] = out_11; immed[15:0] = out_15; opcode[3:0] = out_6;
  //   PCin[15:0] = out_3; r0[15:0] = out_17; r1[15:0] = out_18; r2[15:0] = out_19; r3[15:0] = out_20;
  //   r4[15:0] = out_21; r5[15:0] = out_22; r6[15:0] = out_23; r7[15:0] = out_24; rd[2:0] = out_12; rs[2:0] = out_14;
  //   rt[2:0] = out_13; shAmt[2:0] = out_10

  // Notes on the sheet:
  //   PC+1
  //   Instruction Memory
  //   contents of rom_1 (hex, n*v repeats v):
  //   1048 520d 1240 520d 1240 5209 1240 d01d e028 1048 520d 1240 520d 1243 5209 1241 7280 2558 34a0 4528
  //   5432 6432 14be 6411 a401 410 903f 1fc1 903f 72c0 f600 1241 9601 b01d c038
  //   whereToJump
  //   PC+1+immed
  //   (where to branch to)
  //   Instruction Decoder
  //   Keyboard
  //   Sign Extender
  //   Memory (RAM)
endmodule

module singleRegister (
  input  Clock,
  input  Reset,
  input  [15:0] In,
  input  WriteEnable,
  output [15:0] Out
);

  D_Flip_Flop d_ff_1 (.clk(Clock), .D(In[0]), .Q(Out[0]), .en(WriteEnable), .reset(Reset));  // open: Qn, preset
  D_Flip_Flop d_ff_2 (.clk(Clock), .D(In[1]), .Q(Out[1]), .en(WriteEnable), .reset(Reset));  // open: Qn, preset
  D_Flip_Flop d_ff_3 (.clk(Clock), .D(In[2]), .Q(Out[2]), .en(WriteEnable), .reset(Reset));  // open: Qn, preset
  D_Flip_Flop d_ff_4 (.clk(Clock), .D(In[3]), .Q(Out[3]), .en(WriteEnable), .reset(Reset));  // open: Qn, preset
  D_Flip_Flop d_ff_5 (.clk(Clock), .D(In[4]), .Q(Out[4]), .en(WriteEnable), .reset(Reset));  // open: Qn, preset
  D_Flip_Flop d_ff_6 (.clk(Clock), .D(In[5]), .Q(Out[5]), .en(WriteEnable), .reset(Reset));  // open: Qn, preset
  D_Flip_Flop d_ff_7 (.clk(Clock), .D(In[6]), .Q(Out[6]), .en(WriteEnable), .reset(Reset));  // open: Qn, preset
  D_Flip_Flop d_ff_8 (.clk(Clock), .D(In[7]), .Q(Out[7]), .en(WriteEnable), .reset(Reset));  // open: Qn, preset
  D_Flip_Flop d_ff_9 (.clk(Clock), .D(In[8]), .Q(Out[8]), .en(WriteEnable), .reset(Reset));  // open: Qn, preset
  D_Flip_Flop d_ff_10 (.clk(Clock), .D(In[9]), .Q(Out[9]), .en(WriteEnable), .reset(Reset));  // open: Qn, preset
  D_Flip_Flop d_ff_11 (.clk(Clock), .D(In[10]), .Q(Out[10]), .en(WriteEnable), .reset(Reset));  // open: Qn, preset
  D_Flip_Flop d_ff_12 (.clk(Clock), .D(In[11]), .Q(Out[11]), .en(WriteEnable), .reset(Reset));  // open: Qn, preset
  D_Flip_Flop d_ff_13 (.clk(Clock), .D(In[12]), .Q(Out[12]), .en(WriteEnable), .reset(Reset));  // open: Qn, preset
  D_Flip_Flop d_ff_14 (.clk(Clock), .D(In[13]), .Q(Out[13]), .en(WriteEnable), .reset(Reset));  // open: Qn, preset
  D_Flip_Flop d_ff_15 (.clk(Clock), .D(In[14]), .Q(Out[14]), .en(WriteEnable), .reset(Reset));  // open: Qn, preset
  D_Flip_Flop d_ff_16 (.clk(Clock), .D(In[15]), .Q(Out[15]), .en(WriteEnable), .reset(Reset));  // open: Qn, preset

  // Other names for the same wires on the sheet: _0 = In[0]; _1 = In[1]; _2 = In[2]; _3 = In[3]; _4 = In[4];
  //   _5 = In[5]; _6 = In[6]; _7 = In[7]; _8 = In[8]; _9 = In[9]; _10 = In[10]; _11 = In[11]; _12 = In[12];
  //   _13 = In[13]; _14 = In[14]; _15 = In[15]; x0 = Out[0]; x1 = Out[1]; x2 = Out[2]; x3 = Out[3]; x4 = Out[4];
  //   x5 = Out[5]; x6 = Out[6]; x7 = Out[7]; x8 = Out[8]; x9 = Out[9]; x10 = Out[10]; x11 = Out[11]; x12 = Out[12];
  //   x13 = Out[13]; x14 = Out[14]; x15 = Out[15]; we = WriteEnable
endmodule

module registerFile (
  input  Clock,
  input  Reset,
  input  RegWriteEnable,
  input  [2:0] WriteReg,
  input  [2:0] ReadReg1,
  input  [2:0] ReadReg2,
  input  [15:0] WriteData,
  output [15:0] ReadData1,
  output [15:0] ReadData2,
  output [15:0] reg0,
  output [15:0] reg1,
  output [15:0] reg2,
  output [15:0] reg3,
  output [15:0] reg4,
  output [15:0] reg5,
  output [15:0] reg6,
  output [15:0] reg7
);

  wire WE1, WE2, WE3, WE4, WE5, WE6, WE7;
  wire [15:0] W0, W1, W2, W3, W4, W5, W6, W7;

  Demultiplexer #(.select(3), .width(16)) demultiplexer_1 (
    .out0(W0), .out1(W1), .out2(W2), .out3(W3), .out4(W4), .out5(W5), .out6(W6), .out7(W7), .in(WriteData),
    .sel(WriteReg), .en(RegWriteEnable));
  Decoder #(.select(3), .enable("false")) decoder_1 (
    .out1(WE1), .out2(WE2), .out3(WE3), .out4(WE4), .out5(WE5), .out6(WE6), .out7(WE7), .sel(WriteReg));  // open: out0
  singleRegister R0 (.Clock(Clock), .In({16{1'b0}}), .Reset(Reset), .Out(reg0));  // open: WriteEnable
  singleRegister R4 (.Clock(Clock), .In(W4), .WriteEnable(WE4), .Reset(Reset), .Out(reg4));
  singleRegister R1 (.Clock(Clock), .In(W1), .WriteEnable(WE1), .Reset(Reset), .Out(reg1));
  singleRegister R5 (.Clock(Clock), .In(W5), .WriteEnable(WE5), .Reset(Reset), .Out(reg5));
  singleRegister R2 (.Clock(Clock), .In(W2), .WriteEnable(WE2), .Reset(Reset), .Out(reg2));
  singleRegister R6 (.Clock(Clock), .In(W6), .WriteEnable(WE6), .Reset(Reset), .Out(reg6));
  singleRegister R3 (.Clock(Clock), .In(W3), .WriteEnable(WE3), .Reset(Reset), .Out(reg3));
  singleRegister R7 (.Clock(Clock), .In(W7), .WriteEnable(WE7), .Reset(Reset), .Out(reg7));
  Multiplexer #(.select(3), .width(16), .enable("false")) multiplexer_1 (
    .in0(reg0), .in1(reg1), .in2(reg2), .in3(reg3), .in4(reg4), .in5(reg5), .in6(reg6), .in7(reg7),
    .out(ReadData1), .sel(ReadReg1));
  Multiplexer #(.select(3), .width(16), .enable("false")) multiplexer_2 (
    .in0(reg0), .in1(reg1), .in2(reg2), .in3(reg3), .in4(reg4), .in5(reg5), .in6(reg6), .in7(reg7),
    .out(ReadData2), .sel(ReadReg2));

  // Other names for the same wires on the sheet: A0[15:0] = reg0; A1[15:0] = reg1; A2[15:0] = reg2; A3[15:0] = reg3;
  //   A4[15:0] = reg4; A5[15:0] = reg5; A6[15:0] = reg6; A7[15:0] = reg7; rs1[2:0] = ReadReg1; rs2[2:0] = ReadReg2;
  //   RWE = RegWriteEnable; whichWrite[2:0] = WriteReg
endmodule

module ALU (
  input  [15:0] rs,
  input  [15:0] rt,
  input  [2:0] shiftAmount,
  input  [3:0] opcode,
  output [15:0] OutputData,
  output beq_1001,
  output blt_1010
);

  wire [14:0] sub_0010;
  wire [15:0] add_0000, addi_0001, and_0011, lw_0111, sll_0101, sra_0110, sw_1000, xor_0100;

  _16bitAdder u_16bitadder_1 (.carryIn(1'b0), .InputA(rs), .InputB(rt), .Sum(add_0000));  // open: carryOut
  _16bitAdder u_16bitadder_2 (.carryIn(1'b0), .InputA(rs), .InputB(rt), .Sum(addi_0001));  // open: carryOut
  _16bitAdder u_16bitadder_3 (.carryIn(1'b1), .InputA(rs), .InputB(rt), .Sum({blt_1010, sub_0010}));  // open: carryOut
  assign and_0011 = rs & rt;  // AND_Gate and_1, 16 bits wide
  assign xor_0100 = rs ^ rt;  // XOR_Gate xor_1, 16 bits wide
  shiftLeftLogical_16bit shiftleftlogical_16bit_1 (.Input(rs), .shAmt(shiftAmount), .Output(sll_0101), ._0(1'b0));
  shiftRightArithmetic_16bit shiftrightarithmetic_16bit_1 (
    .Input(rs), .shAmt(shiftAmount), ._0(1'b0), .Output(sra_0110));
  _16bitAdder u_16bitadder_4 (.carryIn(1'b0), .InputA(rs), .InputB(rt), .Sum(lw_0111));  // open: carryOut
  _16bitAdder u_16bitadder_5 (.carryIn(1'b0), .InputA(rs), .InputB(rt), .Sum(sw_1000));  // open: carryOut
  Multiplexer #(.select(4), .width(16), .enable("false")) multiplexer_1 (
    .in0(add_0000), .in1(addi_0001), .in2({blt_1010, sub_0010}), .in3(and_0011), .in4(xor_0100),
    .in5(sll_0101), .in6(sra_0110), .in7(lw_0111), .in8(sw_1000), .out(OutputData), .sel(opcode));  // open: in9, in10, in11, in12, in13, in14, in15
  nor nor_1 (beq_1001, sub_0010[0], sub_0010[1], sub_0010[2], sub_0010[3], sub_0010[4], sub_0010[5], sub_0010[6], sub_0010[7], sub_0010[8], sub_0010[9], sub_0010[10], sub_0010[11], sub_0010[12], sub_0010[13], sub_0010[14], blt_1010);

  // Other names for the same wires on the sheet: shAmt[2:0] = shiftAmount; sub_0010[15] = blt_1010
endmodule

module _16bitAdder (
  input  carryIn,
  input  [15:0] InputA,
  input  [15:0] InputB,
  output [15:0] Sum,
  output carryOut
);

  wire b0, b1, b2, b3, b4, b5, b6, b7, b8, b9, b10, b11, b12, b13, b14, b15, n1bitadder_1_carryout,
       n1bitadder_2_carryout, n1bitadder_3_carryout, n1bitadder_4_carryout, n1bitadder_5_carryout,
       n1bitadder_6_carryout, n1bitadder_7_carryout, n1bitadder_8_carryout, n1bitadder_9_carryout,
       n1bitadder_10_carryout, n1bitadder_11_carryout, n1bitadder_12_carryout, n1bitadder_13_carryout,
       n1bitadder_14_carryout, n1bitadder_15_carryout;

  _1bitAdder u_1bitadder_1 (.A(InputA[0]), .B(b0), .carryIn(carryIn), .Sum(Sum[0]), .carryOut(n1bitadder_1_carryout));
  _1bitAdder u_1bitadder_2 (
    .A(InputA[1]), .B(b1), .carryIn(n1bitadder_1_carryout), .Sum(Sum[1]), .carryOut(n1bitadder_2_carryout));
  _1bitAdder u_1bitadder_3 (
    .A(InputA[2]), .B(b2), .carryIn(n1bitadder_2_carryout), .Sum(Sum[2]), .carryOut(n1bitadder_3_carryout));
  _1bitAdder u_1bitadder_4 (
    .A(InputA[3]), .B(b3), .carryIn(n1bitadder_3_carryout), .Sum(Sum[3]), .carryOut(n1bitadder_4_carryout));
  _1bitAdder u_1bitadder_5 (
    .A(InputA[4]), .B(b4), .carryIn(n1bitadder_4_carryout), .Sum(Sum[4]), .carryOut(n1bitadder_5_carryout));
  _1bitAdder u_1bitadder_6 (
    .A(InputA[5]), .B(b5), .carryIn(n1bitadder_5_carryout), .Sum(Sum[5]), .carryOut(n1bitadder_6_carryout));
  _1bitAdder u_1bitadder_7 (
    .A(InputA[6]), .B(b6), .carryIn(n1bitadder_6_carryout), .Sum(Sum[6]), .carryOut(n1bitadder_7_carryout));
  _1bitAdder u_1bitadder_8 (
    .A(InputA[7]), .B(b7), .carryIn(n1bitadder_7_carryout), .Sum(Sum[7]), .carryOut(n1bitadder_8_carryout));
  _1bitAdder u_1bitadder_9 (
    .A(InputA[8]), .B(b8), .carryIn(n1bitadder_8_carryout), .Sum(Sum[8]), .carryOut(n1bitadder_9_carryout));
  _1bitAdder u_1bitadder_10 (
    .A(InputA[9]), .B(b9), .carryIn(n1bitadder_9_carryout), .Sum(Sum[9]), .carryOut(n1bitadder_10_carryout));
  _1bitAdder u_1bitadder_11 (
    .A(InputA[10]), .B(b10), .carryIn(n1bitadder_10_carryout), .Sum(Sum[10]),
    .carryOut(n1bitadder_11_carryout));
  _1bitAdder u_1bitadder_12 (
    .A(InputA[11]), .B(b11), .carryIn(n1bitadder_11_carryout), .Sum(Sum[11]),
    .carryOut(n1bitadder_12_carryout));
  _1bitAdder u_1bitadder_13 (
    .A(InputA[12]), .B(b12), .carryIn(n1bitadder_12_carryout), .Sum(Sum[12]),
    .carryOut(n1bitadder_13_carryout));
  _1bitAdder u_1bitadder_14 (
    .A(InputA[13]), .B(b13), .carryIn(n1bitadder_13_carryout), .Sum(Sum[13]),
    .carryOut(n1bitadder_14_carryout));
  _1bitAdder u_1bitadder_15 (
    .A(InputA[14]), .B(b14), .carryIn(n1bitadder_14_carryout), .Sum(Sum[14]),
    .carryOut(n1bitadder_15_carryout));
  _1bitAdder u_1bitadder_16 (
    .A(InputA[15]), .B(b15), .carryIn(n1bitadder_15_carryout), .Sum(Sum[15]), .carryOut(carryOut));
  xor xor_1 (b0, InputB[0], carryIn);
  xor xor_2 (b1, InputB[1], carryIn);
  xor xor_3 (b2, InputB[2], carryIn);
  xor xor_4 (b3, InputB[3], carryIn);
  xor xor_5 (b4, InputB[4], carryIn);
  xor xor_6 (b5, InputB[5], carryIn);
  xor xor_7 (b6, InputB[6], carryIn);
  xor xor_8 (b7, InputB[7], carryIn);
  xor xor_9 (b8, InputB[8], carryIn);
  xor xor_10 (b9, InputB[9], carryIn);
  xor xor_11 (b10, InputB[10], carryIn);
  xor xor_12 (b11, InputB[11], carryIn);
  xor xor_13 (b12, InputB[12], carryIn);
  xor xor_14 (b13, InputB[13], carryIn);
  xor xor_15 (b14, InputB[14], carryIn);
  xor xor_16 (b15, InputB[15], carryIn);

  // Other names for the same wires on the sheet: a0 = InputA[0]; a1 = InputA[1]; a2 = InputA[2]; a3 = InputA[3];
  //   a4 = InputA[4]; a5 = InputA[5]; a6 = InputA[6]; a7 = InputA[7]; a8 = InputA[8]; a9 = InputA[9];
  //   a10 = InputA[10]; a11 = InputA[11]; a12 = InputA[12]; a13 = InputA[13]; a14 = InputA[14]; a15 = InputA[15];
  //   _0 = InputB[0]; _1 = InputB[1]; _2 = InputB[2]; _3 = InputB[3]; _4 = InputB[4]; _5 = InputB[5]; _6 = InputB[6];
  //   _7 = InputB[7]; _8 = InputB[8]; _9 = InputB[9]; _10 = InputB[10]; _11 = InputB[11]; _12 = InputB[12];
  //   _13 = InputB[13]; _14 = InputB[14]; _15 = InputB[15]
endmodule

module _1bitAdder (
  input  A,
  input  B,
  input  carryIn,
  output Sum,
  output carryOut
);

  wire and_1_out, and_2_out, and_3_out, and_4_out, and_5_out, and_6_out, and_7_out, not_1_out, not_2_out,
       not_3_out;

  not not_1 (not_1_out, A);
  not not_2 (not_2_out, B);
  not not_3 (not_3_out, carryIn);
  and and_1 (and_1_out, not_1_out, not_2_out, carryIn);
  and and_2 (and_2_out, not_1_out, B, not_3_out);
  and and_3 (and_3_out, A, not_2_out, not_3_out);
  and and_4 (and_4_out, A, B, carryIn);
  and and_5 (and_5_out, B, carryIn);
  and and_6 (and_6_out, B, A);
  and and_7 (and_7_out, carryIn, A);
  or or_1 (Sum, and_1_out, and_2_out, and_3_out, and_4_out);
  or or_2 (carryOut, and_5_out, and_6_out, and_7_out);
endmodule

module shiftLeftLogical_16bit (
  input  [15:0] Input,
  input  [2:0] shAmt,
  input  _0,
  output [15:0] Output
);

  wire [15:0] shiftleftlogical_1bit_1_out, shiftleftlogical_1bit_2_out, shiftleftlogical_1bit_3_out,
       shiftleftlogical_1bit_4_out, shiftleftlogical_1bit_5_out, shiftleftlogical_1bit_6_out;

  shiftLeftLogical_1bit shiftleftlogical_1bit_1 (
    .InputA(Input), .shiftAmount(shAmt[0]), ._0(_0), .out(shiftleftlogical_1bit_1_out));
  shiftLeftLogical_1bit shiftleftlogical_1bit_2 (
    .InputA(shiftleftlogical_1bit_1_out), .shiftAmount(shAmt[1]), ._0(_0), .out(shiftleftlogical_1bit_2_out));
  shiftLeftLogical_1bit shiftleftlogical_1bit_3 (
    .InputA(shiftleftlogical_1bit_2_out), .shiftAmount(shAmt[1]), ._0(_0), .out(shiftleftlogical_1bit_3_out));
  shiftLeftLogical_1bit shiftleftlogical_1bit_4 (
    .InputA(shiftleftlogical_1bit_3_out), .shiftAmount(shAmt[2]), ._0(_0), .out(shiftleftlogical_1bit_4_out));
  shiftLeftLogical_1bit shiftleftlogical_1bit_5 (
    .InputA(shiftleftlogical_1bit_4_out), .shiftAmount(shAmt[2]), ._0(_0), .out(shiftleftlogical_1bit_5_out));
  shiftLeftLogical_1bit shiftleftlogical_1bit_6 (
    .InputA(shiftleftlogical_1bit_5_out), .shiftAmount(shAmt[2]), ._0(_0), .out(shiftleftlogical_1bit_6_out));
  shiftLeftLogical_1bit shiftleftlogical_1bit_7 (
    .InputA(shiftleftlogical_1bit_6_out), .shiftAmount(shAmt[2]), ._0(_0), .out(Output));

  // Other names for the same wires on the sheet: sh0 = shAmt[0]; sh1 = shAmt[1]; sh2 = shAmt[2]
endmodule

module shiftLeftLogical_1bit (
  input  [15:0] InputA,
  input  shiftAmount,
  input  _0,
  output [15:0] out
);

  Multiplexer multiplexer_1 (.in0(InputA[15]), .in1(InputA[14]), .out(out[15]), .sel(shiftAmount));  // open: en
  Multiplexer multiplexer_2 (.in0(InputA[14]), .in1(InputA[13]), .out(out[14]), .sel(shiftAmount));  // open: en
  Multiplexer multiplexer_3 (.in0(InputA[13]), .in1(InputA[12]), .out(out[13]), .sel(shiftAmount));  // open: en
  Multiplexer multiplexer_4 (.in0(InputA[12]), .in1(InputA[11]), .out(out[12]), .sel(shiftAmount));  // open: en
  Multiplexer multiplexer_5 (.in0(InputA[11]), .in1(InputA[10]), .out(out[11]), .sel(shiftAmount));  // open: en
  Multiplexer multiplexer_6 (.in0(InputA[10]), .in1(InputA[9]), .out(out[10]), .sel(shiftAmount));  // open: en
  Multiplexer multiplexer_7 (.in0(InputA[9]), .in1(InputA[8]), .out(out[9]), .sel(shiftAmount));  // open: en
  Multiplexer multiplexer_8 (.in0(InputA[8]), .in1(InputA[7]), .out(out[8]), .sel(shiftAmount));  // open: en
  Multiplexer multiplexer_9 (.in0(InputA[7]), .in1(InputA[6]), .out(out[7]), .sel(shiftAmount));  // open: en
  Multiplexer multiplexer_10 (.in0(InputA[6]), .in1(InputA[5]), .out(out[6]), .sel(shiftAmount));  // open: en
  Multiplexer multiplexer_11 (.in0(InputA[5]), .in1(InputA[4]), .out(out[5]), .sel(shiftAmount));  // open: en
  Multiplexer multiplexer_12 (.in0(InputA[4]), .in1(InputA[3]), .out(out[4]), .sel(shiftAmount));  // open: en
  Multiplexer multiplexer_13 (.in0(InputA[3]), .in1(InputA[2]), .out(out[3]), .sel(shiftAmount));  // open: en
  Multiplexer multiplexer_14 (.in0(InputA[2]), .in1(InputA[1]), .out(out[2]), .sel(shiftAmount));  // open: en
  Multiplexer multiplexer_15 (.in0(InputA[1]), .in1(InputA[0]), .out(out[1]), .sel(shiftAmount));  // open: en
  Multiplexer multiplexer_16 (.in0(InputA[0]), .in1(_0), .out(out[0]), .sel(shiftAmount));  // open: en

  // Other names for the same wires on the sheet: a0 = InputA[0]; a1 = InputA[1]; a2 = InputA[2]; a3 = InputA[3];
  //   a4 = InputA[4]; a5 = InputA[5]; a6 = InputA[6]; a7 = InputA[7]; a8 = InputA[8]; a9 = InputA[9];
  //   a10 = InputA[10]; a11 = InputA[11]; a12 = InputA[12]; a13 = InputA[13]; a14 = InputA[14]; a15 = InputA[15];
  //   shAmt = shiftAmount
endmodule

module shiftRightArithmetic_1bit (
  input  [15:0] InputA,
  input  shiftAmount,
  input  in_3,
  output [15:0] out
);

  Multiplexer multiplexer_1 (.in0(InputA[0]), .in1(InputA[1]), .out(out[0]), .sel(shiftAmount));  // open: en
  Multiplexer multiplexer_2 (.in0(InputA[1]), .in1(InputA[2]), .out(out[1]), .sel(shiftAmount));  // open: en
  Multiplexer multiplexer_3 (.in0(InputA[2]), .in1(InputA[3]), .out(out[2]), .sel(shiftAmount));  // open: en
  Multiplexer multiplexer_4 (.in0(InputA[3]), .in1(InputA[4]), .out(out[3]), .sel(shiftAmount));  // open: en
  Multiplexer multiplexer_5 (.in0(InputA[4]), .in1(InputA[5]), .out(out[4]), .sel(shiftAmount));  // open: en
  Multiplexer multiplexer_6 (.in0(InputA[5]), .in1(InputA[6]), .out(out[5]), .sel(shiftAmount));  // open: en
  Multiplexer multiplexer_7 (.in0(InputA[6]), .in1(InputA[7]), .out(out[6]), .sel(shiftAmount));  // open: en
  Multiplexer multiplexer_8 (.in0(InputA[7]), .in1(InputA[8]), .out(out[7]), .sel(shiftAmount));  // open: en
  Multiplexer multiplexer_9 (.in0(InputA[8]), .in1(InputA[9]), .out(out[8]), .sel(shiftAmount));  // open: en
  Multiplexer multiplexer_10 (.in0(InputA[9]), .in1(InputA[10]), .out(out[9]), .sel(shiftAmount));  // open: en
  Multiplexer multiplexer_11 (.in0(InputA[10]), .in1(InputA[11]), .out(out[10]), .sel(shiftAmount));  // open: en
  Multiplexer multiplexer_12 (.in0(InputA[11]), .in1(InputA[12]), .out(out[11]), .sel(shiftAmount));  // open: en
  Multiplexer multiplexer_13 (.in0(InputA[12]), .in1(InputA[13]), .out(out[12]), .sel(shiftAmount));  // open: en
  Multiplexer multiplexer_14 (.in0(InputA[13]), .in1(InputA[14]), .out(out[13]), .sel(shiftAmount));  // open: en
  Multiplexer multiplexer_15 (.in0(InputA[14]), .in1(in_3), .out(out[14]), .sel(shiftAmount));  // open: en
  Multiplexer multiplexer_16 (.in0(InputA[15]), .in1(InputA[15]), .out(out[15]), .sel(shiftAmount));  // open: en

  // Other names for the same wires on the sheet: a0 = InputA[0]; a1 = InputA[1]; a2 = InputA[2]; a3 = InputA[3];
  //   a4 = InputA[4]; a5 = InputA[5]; a6 = InputA[6]; a7 = InputA[7]; a8 = InputA[8]; a9 = InputA[9];
  //   a10 = InputA[10]; a11 = InputA[11]; a12 = InputA[12]; a13 = InputA[13]; a14 = InputA[14]; a15 = InputA[15];
  //   shAmt = shiftAmount
endmodule

module shiftRightArithmetic_16bit (
  input  [15:0] Input,
  input  [2:0] shAmt,
  input  _0,
  output [15:0] Output
);

  wire [15:0] shiftrightarithmetic_1bit_1_out, shiftrightarithmetic_1bit_2_out,
       shiftrightarithmetic_1bit_3_out, shiftrightarithmetic_1bit_4_out, shiftrightarithmetic_1bit_5_out,
       shiftrightarithmetic_1bit_6_out;

  shiftRightArithmetic_1bit shiftrightarithmetic_1bit_1 (
    .InputA(Input), .shiftAmount(shAmt[0]), .in_3(_0), .out(shiftrightarithmetic_1bit_1_out));
  shiftRightArithmetic_1bit shiftrightarithmetic_1bit_2 (
    .InputA(shiftrightarithmetic_1bit_1_out), .shiftAmount(shAmt[1]), .in_3(_0),
    .out(shiftrightarithmetic_1bit_2_out));
  shiftRightArithmetic_1bit shiftrightarithmetic_1bit_3 (
    .InputA(shiftrightarithmetic_1bit_2_out), .shiftAmount(shAmt[1]), .in_3(_0),
    .out(shiftrightarithmetic_1bit_3_out));
  shiftRightArithmetic_1bit shiftrightarithmetic_1bit_4 (
    .InputA(shiftrightarithmetic_1bit_3_out), .shiftAmount(shAmt[2]), .in_3(_0),
    .out(shiftrightarithmetic_1bit_4_out));
  shiftRightArithmetic_1bit shiftrightarithmetic_1bit_5 (
    .InputA(shiftrightarithmetic_1bit_4_out), .shiftAmount(shAmt[2]), .in_3(_0),
    .out(shiftrightarithmetic_1bit_5_out));
  shiftRightArithmetic_1bit shiftrightarithmetic_1bit_6 (
    .InputA(shiftrightarithmetic_1bit_5_out), .shiftAmount(shAmt[2]), .in_3(_0),
    .out(shiftrightarithmetic_1bit_6_out));
  shiftRightArithmetic_1bit shiftrightarithmetic_1bit_7 (
    .InputA(shiftrightarithmetic_1bit_6_out), .shiftAmount(shAmt[2]), .in_3(_0), .out(Output));

  // Other names for the same wires on the sheet: sh0 = shAmt[0]; sh1 = shAmt[1]; sh2 = shAmt[2]
endmodule

module PC (
  input  Clock,
  input  Reset,
  input  [15:0] In,
  output [15:0] Out
);

  wire clock_1_out;

  Clock clock_1 (.out(clock_1_out));
  D_Flip_Flop d_ff_1 (.clk(clock_1_out), .D(In[0]), .Q(Out[0]), .reset(Reset));  // open: Qn, preset, en
  D_Flip_Flop d_ff_2 (.clk(clock_1_out), .D(In[1]), .Q(Out[1]), .reset(Reset));  // open: Qn, preset, en
  D_Flip_Flop d_ff_3 (.clk(clock_1_out), .D(In[2]), .Q(Out[2]), .reset(Reset));  // open: Qn, preset, en
  D_Flip_Flop d_ff_4 (.clk(clock_1_out), .D(In[3]), .Q(Out[3]), .reset(Reset));  // open: Qn, preset, en
  D_Flip_Flop d_ff_5 (.clk(clock_1_out), .D(In[4]), .Q(Out[4]), .reset(Reset));  // open: Qn, preset, en
  D_Flip_Flop d_ff_6 (.clk(clock_1_out), .D(In[5]), .Q(Out[5]), .reset(Reset));  // open: Qn, preset, en
  D_Flip_Flop d_ff_7 (.clk(clock_1_out), .D(In[6]), .Q(Out[6]), .reset(Reset));  // open: Qn, preset, en
  D_Flip_Flop d_ff_8 (.clk(clock_1_out), .D(In[7]), .Q(Out[7]), .reset(Reset));  // open: Qn, preset, en
  D_Flip_Flop d_ff_9 (.clk(clock_1_out), .D(In[8]), .Q(Out[8]), .reset(Reset));  // open: Qn, preset, en
  D_Flip_Flop d_ff_10 (.clk(clock_1_out), .D(In[9]), .Q(Out[9]), .reset(Reset));  // open: Qn, preset, en
  D_Flip_Flop d_ff_11 (.clk(clock_1_out), .D(In[10]), .Q(Out[10]), .reset(Reset));  // open: Qn, preset, en
  D_Flip_Flop d_ff_12 (.clk(clock_1_out), .D(In[11]), .Q(Out[11]), .reset(Reset));  // open: Qn, preset, en
  D_Flip_Flop d_ff_13 (.clk(clock_1_out), .D(In[12]), .Q(Out[12]), .reset(Reset));  // open: Qn, preset, en
  D_Flip_Flop d_ff_14 (.clk(clock_1_out), .D(In[13]), .Q(Out[13]), .reset(Reset));  // open: Qn, preset, en
  D_Flip_Flop d_ff_15 (.clk(clock_1_out), .D(In[14]), .Q(Out[14]), .reset(Reset));  // open: Qn, preset, en
  D_Flip_Flop d_ff_16 (.clk(clock_1_out), .D(In[15]), .Q(Out[15]), .reset(Reset));  // open: Qn, preset, en

  // Other names for the same wires on the sheet: _0 = In[0]; _1 = In[1]; _2 = In[2]; _3 = In[3]; _4 = In[4];
  //   _5 = In[5]; _6 = In[6]; _7 = In[7]; _8 = In[8]; _9 = In[9]; _10 = In[10]; _11 = In[11]; _12 = In[12];
  //   _13 = In[13]; _14 = In[14]; _15 = In[15]; x0 = Out[0]; x1 = Out[1]; x2 = Out[2]; x3 = Out[3]; x4 = Out[4];
  //   x5 = Out[5]; x6 = Out[6]; x7 = Out[7]; x8 = Out[8]; x9 = Out[9]; x10 = Out[10]; x11 = Out[11]; x12 = Out[12];
  //   x13 = Out[13]; x14 = Out[14]; x15 = Out[15]
endmodule

module Instruction_Splitter (
  input  [15:0] instruction,
  output [2:0] shAmt,
  output [2:0] rd,
  output [2:0] rt,
  output [2:0] rs,
  output [3:0] opcode,
  output [11:0] address,
  output [15:0] immed
);

  SX_6_t0_16 sx_6_t0_16_1 (.immed(instruction[5:0]), .sxImmed(immed));

  assign address = instruction[11:0];
  assign opcode = instruction[15:12];
  assign rd = instruction[5:3];
  assign rs = instruction[11:9];
  assign rt = instruction[8:6];
  assign shAmt = instruction[2:0];

  // Other names for the same wires on the sheet: _0 = instruction[0]; _1 = instruction[1]; _2 = instruction[2];
  //   _3 = instruction[3]; _4 = instruction[4]; _5 = instruction[5]; _6 = instruction[6]; _7 = instruction[7];
  //   _8 = instruction[8]; _9 = instruction[9]; _10 = instruction[10]; _11 = instruction[11]; _12 = instruction[12];
  //   _13 = instruction[13]; _14 = instruction[14]; _15 = instruction[15]
endmodule

module Control (
  input  [3:0] opcode,
  output regDest,
  output writingReg,
  output aluImm,
  output branch,
  output memToReg,
  output writeMem,
  output j,
  output jal,
  output jr,
  output \input ,
  output \output ,
  output beq
);

  wire add, addi, \and , blt, sll, sra, sub, \xor ;

  and _0000 (add, ~opcode[0], ~opcode[1], ~opcode[2], ~opcode[3]);  // AND_Gate
  and _0001 (addi, opcode[0], ~opcode[1], ~opcode[2], ~opcode[3]);  // AND_Gate
  and _0010 (sub, ~opcode[0], opcode[1], ~opcode[2], ~opcode[3]);  // AND_Gate
  and _0011 (\and , opcode[0], opcode[1], ~opcode[2], ~opcode[3]);  // AND_Gate
  and _0100 (\xor , ~opcode[0], ~opcode[1], opcode[2], ~opcode[3]);  // AND_Gate
  and _0101 (sll, opcode[0], ~opcode[1], opcode[2], ~opcode[3]);  // AND_Gate
  and _0110 (sra, ~opcode[0], opcode[1], opcode[2], ~opcode[3]);  // AND_Gate
  and _0111 (memToReg, opcode[0], opcode[1], opcode[2], ~opcode[3]);  // AND_Gate
  and _1000 (writeMem, ~opcode[0], ~opcode[1], ~opcode[2], opcode[3]);  // AND_Gate
  and _1001 (beq, opcode[0], ~opcode[1], ~opcode[2], opcode[3]);  // AND_Gate
  and _1010 (blt, ~opcode[0], opcode[1], ~opcode[2], opcode[3]);  // AND_Gate
  and _1011 (j, opcode[0], opcode[1], ~opcode[2], opcode[3]);  // AND_Gate
  and _1100 (jr, ~opcode[0], ~opcode[1], opcode[2], opcode[3]);  // AND_Gate
  and _1101 (jal, opcode[0], ~opcode[1], opcode[2], opcode[3]);  // AND_Gate
  and _1110 (\input , ~opcode[0], opcode[1], opcode[2], opcode[3]);  // AND_Gate
  and _1111 (\output , opcode[0], opcode[1], opcode[2], opcode[3]);
  or or_1 (aluImm, addi, memToReg, writeMem);
  or or_2 (regDest, add, sub, \xor , sll, sra, jal, \and );
  or or_3 (branch, beq, blt);
  or or_4 (writingReg, add, addi, sub, \and , jal, \xor , sll, sra, memToReg, \input );

  // Other names for the same wires on the sheet: lw = memToReg; _0 = opcode[0]; _1 = opcode[1]; _2 = opcode[2];
  //   _3 = opcode[3]; sw = writeMem
endmodule

module SX_6_t0_16 (
  input  [5:0] immed,
  output [15:0] sxImmed
);


  assign sxImmed = {{11{immed[5]}}, immed[4:0]};
endmodule

module nonZero (
  input  [15:0] Din,
  output isNonZero
);

  or or_1 (isNonZero, Din[0], Din[1], Din[2], Din[3], Din[4], Din[5], Din[6], Din[7], Din[8], Din[9], Din[10], Din[11], Din[12], Din[13], Din[14], Din[15]);
endmodule
