// Logisim project BrianLinCPUhomework4.circ as structural Verilog: 5 circuits, main circuit singleRegister
module singleRegister (
  input  Reset,
  input  [15:0] In,
  output [15:0] Out
);

  wire clock_1_out, x1;

  Clock clock_1 (.out(clock_1_out));
  D_Flip_Flop d_ff_1 (.clk(clock_1_out), .D(In[0]), .Q(Out[0]), .reset(Reset));  // open: Qn, preset, en
  D_Flip_Flop d_ff_2 (.clk(clock_1_out), .D(In[1]), .Q(x1), .reset(Reset));  // open: Qn, preset, en
  D_Flip_Flop d_ff_3 (.clk(clock_1_out), .D(In[2]), .Q(Out[2]), .reset(Reset));  // open: Qn, preset, en
  D_Flip_Flop d_ff_4 (.clk(clock_1_out), .D(In[3]), .Q(Out[3]));  // open: Qn, preset, en, reset
  D_Flip_Flop d_ff_5 (.clk(clock_1_out), .D(In[4]), .Q(Out[4]), .reset(Reset));  // open: Qn, preset, en
  D_Flip_Flop d_ff_6 (.clk(clock_1_out), .D(In[5]), .Q(Out[5]), .reset(Reset));  // open: Qn, preset, en
  D_Flip_Flop d_ff_7 (.clk(clock_1_out), .D(In[6]), .Q(Out[6]), .reset(Reset));  // open: Qn, preset, en
  D_Flip_Flop d_ff_8 (.clk(clock_1_out), .D(In[7]), .Q(Out[7]));  // open: Qn, preset, en, reset
  D_Flip_Flop d_ff_9 (.clk(clock_1_out), .D(In[8]), .Q(Out[8]), .reset(Reset));  // open: Qn, preset, en
  D_Flip_Flop d_ff_10 (.clk(clock_1_out), .D(In[9]), .Q(Out[9]), .reset(Reset));  // open: Qn, preset, en
  D_Flip_Flop d_ff_11 (.clk(clock_1_out), .D(In[10]), .Q(Out[10]), .reset(Reset));  // open: Qn, preset, en
  D_Flip_Flop d_ff_12 (.clk(clock_1_out), .D(In[11]), .Q(Out[11]));  // open: Qn, preset, en, reset
  D_Flip_Flop d_ff_13 (.clk(clock_1_out), .D(In[12]), .Q(Out[12]), .reset(Reset));  // open: Qn, preset, en
  D_Flip_Flop d_ff_14 (.clk(clock_1_out), .D(In[13]), .Q(Out[13]), .reset(Reset));  // open: Qn, preset, en
  D_Flip_Flop d_ff_15 (.clk(clock_1_out), .D(In[14]), .Q(Out[14]), .reset(Reset));  // open: Qn, preset, en
  D_Flip_Flop d_ff_16 (.clk(clock_1_out), .D(In[15]), .Q(Out[15]));  // open: Qn, preset, en, reset

  assign Out[1] = Out[2];

  // Other names for the same wires on the sheet: _0 = In[0]; _1 = In[1]; _2 = In[2]; _3 = In[3]; _4 = In[4];
  //   _5 = In[5]; _6 = In[6]; _7 = In[7]; _8 = In[8]; _9 = In[9]; _10 = In[10]; _11 = In[11]; _12 = In[12];
  //   _13 = In[13]; _14 = In[14]; _15 = In[15]; x0 = Out[0]; x2 = Out[2]; x3 = Out[3]; x4 = Out[4]; x5 = Out[5];
  //   x6 = Out[6]; x7 = Out[7]; x8 = Out[8]; x9 = Out[9]; x10 = Out[10]; x11 = Out[11]; x12 = Out[12]; x13 = Out[13];
  //   x14 = Out[14]; x15 = Out[15]
endmodule

module registerFile (
  input  Reset,
  input  RegWriteEnable,
  input  [3:0] WriteReg,
  input  [3:0] ReadReg1,
  input  [15:0] WriteData,
  output [15:0] ReadData1
);

  wire [15:0] A0, A1, A2, A3, A4, A5, A6, A7, A8, A9, A10, A11, A12, A13, A14, A15, W0, W1, W2, W3, W4, W5,
       W6, W7, W8, W9, W10, W11, W12, W13, W14, W15;

  Demultiplexer #(.select(4), .width(16)) demultiplexer_1 (
    .out0(W0), .out1(W1), .out2(W2), .out3(W3), .out4(W4), .out5(W5), .out6(W6), .out7(W7), .out8(W8),
    .out9(W9), .out10(W10), .out11(W11), .out12(W12), .out13(W13), .out14(W14), .out15(W15), .in(WriteData),
    .sel(WriteReg), .en(RegWriteEnable));
  singleRegister R0 (.In({16{1'b0}}), .Reset(Reset), .Out(A0));
  singleRegister R4 (.In(W4), .Reset(Reset), .Out(A4));
  singleRegister R8 (.In(W8), .Reset(Reset), .Out(A8));
  singleRegister R12 (.In(W12), .Reset(Reset), .Out(A12));
  singleRegister R1 (.In(W1), .Reset(Reset), .Out(A1));
  singleRegister R5 (.In(W5), .Reset(Reset), .Out(A5));
  singleRegister R9 (.In(W9), .Reset(Reset), .Out(A9));
  singleRegister R13 (.In(W13), .Reset(Reset), .Out(A13));
  singleRegister R2 (.In(W2), .Reset(Reset), .Out(A2));
  singleRegister R6 (.In(W6), .Reset(Reset), .Out(A6));
  singleRegister R10 (.In(W10), .Reset(Reset), .Out(A10));
  singleRegister R14 (.In(W14), .Reset(Reset), .Out(A14));
  singleRegister R3 (.In(W3), .Reset(Reset), .Out(A3));
  singleRegister R7 (.In(W7), .Reset(Reset), .Out(A7));
  singleRegister R11 (.In(W11), .Reset(Reset), .Out(A11));
  singleRegister R15 (.In(W15), .Reset(Reset), .Out(A15));
  Multiplexer #(.select(4), .width(16), .enable("false")) multiplexer_1 (
    .in0(A0), .in1(A1), .in2(A2), .in3(A3), .in4(A4), .in5(A5), .in6(A6), .in7(A7), .in8(A8), .in9(A9),
    .in10(A10), .in11(A11), .in12(A12), .in13(A13), .in14(A14), .in15(A15), .out(ReadData1), .sel(ReadReg1));

  // Other names for the same wires on the sheet: aIn[3:0] = ReadReg1; RWE = RegWriteEnable;
  //   whichWrite[3:0] = WriteReg

  // Notes on the sheet:
  //   A-Out
endmodule

module ALU (
  input  [3:0] Opcode,
  input  [15:0] InputData1,
  input  [15:0] InputData2,
  output [15:0] OutputData
);
endmodule

module _16bitAdder (
  input  carryIn,
  input  [15:0] InputA,
  input  [15:0] InputB,
  output [15:0] Sum,
  output carryOut
);

  wire n1bitadder_1_carryout, n1bitadder_2_carryout, n1bitadder_3_carryout, n1bitadder_4_carryout,
       n1bitadder_5_carryout, n1bitadder_6_carryout, n1bitadder_7_carryout, n1bitadder_8_carryout,
       n1bitadder_9_carryout, n1bitadder_10_carryout, n1bitadder_11_carryout, n1bitadder_12_carryout,
       n1bitadder_13_carryout, n1bitadder_14_carryout, n1bitadder_15_carryout;

  _1bitAdder u_1bitadder_1 (
    .A(InputA[0]), .B(InputB[0]), .carryIn(carryIn), .Sum(Sum[0]), .carryOut(n1bitadder_1_carryout));
  _1bitAdder u_1bitadder_2 (
    .A(InputA[1]), .B(InputB[1]), .carryIn(n1bitadder_1_carryout), .Sum(Sum[1]),
    .carryOut(n1bitadder_2_carryout));
  _1bitAdder u_1bitadder_3 (
    .A(InputA[2]), .B(InputB[2]), .carryIn(n1bitadder_2_carryout), .Sum(Sum[2]),
    .carryOut(n1bitadder_3_carryout));
  _1bitAdder u_1bitadder_4 (
    .A(InputA[3]), .B(InputB[3]), .carryIn(n1bitadder_3_carryout), .Sum(Sum[3]),
    .carryOut(n1bitadder_4_carryout));
  _1bitAdder u_1bitadder_5 (
    .A(InputA[4]), .B(InputB[4]), .carryIn(n1bitadder_4_carryout), .Sum(Sum[4]),
    .carryOut(n1bitadder_5_carryout));
  _1bitAdder u_1bitadder_6 (
    .A(InputA[5]), .B(InputB[5]), .carryIn(n1bitadder_5_carryout), .Sum(Sum[5]),
    .carryOut(n1bitadder_6_carryout));
  _1bitAdder u_1bitadder_7 (
    .A(InputA[6]), .B(InputB[6]), .carryIn(n1bitadder_6_carryout), .Sum(Sum[6]),
    .carryOut(n1bitadder_7_carryout));
  _1bitAdder u_1bitadder_8 (
    .A(InputA[7]), .B(InputB[7]), .carryIn(n1bitadder_7_carryout), .Sum(Sum[7]),
    .carryOut(n1bitadder_8_carryout));
  _1bitAdder u_1bitadder_9 (
    .A(InputA[8]), .B(InputB[8]), .carryIn(n1bitadder_8_carryout), .Sum(Sum[8]),
    .carryOut(n1bitadder_9_carryout));
  _1bitAdder u_1bitadder_10 (
    .A(InputA[9]), .B(InputB[9]), .carryIn(n1bitadder_9_carryout), .Sum(Sum[9]),
    .carryOut(n1bitadder_10_carryout));
  _1bitAdder u_1bitadder_11 (
    .A(InputA[10]), .B(InputB[10]), .carryIn(n1bitadder_10_carryout), .Sum(Sum[10]),
    .carryOut(n1bitadder_11_carryout));
  _1bitAdder u_1bitadder_12 (
    .A(InputA[11]), .B(InputB[11]), .carryIn(n1bitadder_11_carryout), .Sum(Sum[11]),
    .carryOut(n1bitadder_12_carryout));
  _1bitAdder u_1bitadder_13 (
    .A(InputA[12]), .B(InputB[12]), .carryIn(n1bitadder_12_carryout), .Sum(Sum[12]),
    .carryOut(n1bitadder_13_carryout));
  _1bitAdder u_1bitadder_14 (
    .A(InputA[13]), .B(InputB[13]), .carryIn(n1bitadder_13_carryout), .Sum(Sum[13]),
    .carryOut(n1bitadder_14_carryout));
  _1bitAdder u_1bitadder_15 (
    .A(InputA[14]), .B(InputB[14]), .carryIn(n1bitadder_14_carryout), .Sum(Sum[14]),
    .carryOut(n1bitadder_15_carryout));
  _1bitAdder u_1bitadder_16 (
    .A(InputA[15]), .B(InputB[15]), .carryIn(n1bitadder_15_carryout), .Sum(Sum[15]), .carryOut(carryOut));

  // Other names for the same wires on the sheet: a0 = InputA[0]; a1 = InputA[1]; a2 = InputA[2]; a3 = InputA[3];
  //   a4 = InputA[4]; a5 = InputA[5]; a6 = InputA[6]; a7 = InputA[7]; a8 = InputA[8]; a9 = InputA[9];
  //   a10 = InputA[10]; a11 = InputA[11]; a12 = InputA[12]; a13 = InputA[13]; a14 = InputA[14]; a15 = InputA[15];
  //   b0 = InputB[0]; b1 = InputB[1]; b2 = InputB[2]; b3 = InputB[3]; b4 = InputB[4]; b5 = InputB[5]; b6 = InputB[6];
  //   b7 = InputB[7]; b8 = InputB[8]; b9 = InputB[9]; b10 = InputB[10]; b11 = InputB[11]; b12 = InputB[12];
  //   b13 = InputB[13]; b14 = InputB[14]; b15 = InputB[15]
endmodule

module _1bitAdder (
  input  A,
  input  B,
  input  carryIn,
  output Sum,
  output carryOut
);

  wire and_1_out, and_2_out, and_3_out, and_4_out, and_5_out, and_6_out, and_7_out, not_1_out, not_2_out,
       not_3_out;

  not not_1 (not_1_out, A);
  not not_2 (not_2_out, B);
  not not_3 (not_3_out, carryIn);
  and and_1 (and_1_out, not_1_out, not_2_out, carryIn);
  and and_2 (and_2_out, not_1_out, B, not_3_out);
  and and_3 (and_3_out, A, not_2_out, not_3_out);
  and and_4 (and_4_out, A, B, carryIn);
  and and_5 (and_5_out, B, carryIn);
  and and_6 (and_6_out, B, A);
  and and_7 (and_7_out, carryIn, A);
  or or_1 (Sum, and_1_out, and_2_out, and_3_out, and_4_out);
  or or_2 (carryOut, and_5_out, and_6_out, and_7_out);
endmodule
