// Logisim project recitation.circ as structural Verilog: 1 circuit, main circuit main
module main (
  input  [7:0] in_1,
  input  [7:0] in_2
);

  D_Flip_Flop d_ff_1 (.D(in_1[0]));  // open: clk, Q, Qn, preset, en, reset
  D_Flip_Flop d_ff_2 ();  // open: clk, D, Q, Qn, preset, en, reset
  D_Flip_Flop d_ff_3 (.D(in_1[1]));  // open: clk, Q, Qn, preset, en, reset
  D_Flip_Flop d_ff_4 ();  // open: clk, D, Q, Qn, preset, en, reset
  D_Flip_Flop d_ff_5 (.D(in_1[2]));  // open: clk, Q, Qn, preset, en, reset
  D_Flip_Flop d_ff_6 ();  // open: clk, D, Q, Qn, preset, en, reset
  D_Flip_Flop d_ff_7 (.D(in_1[3]));  // open: clk, Q, Qn, preset, en, reset
  D_Flip_Flop d_ff_8 ();  // open: clk, D, Q, Qn, preset, en, reset
  D_Flip_Flop d_ff_9 (.D(in_1[4]));  // open: clk, Q, Qn, preset, en, reset
  D_Flip_Flop d_ff_10 ();  // open: clk, D, Q, Qn, preset, en, reset
  D_Flip_Flop d_ff_11 (.D(in_1[5]));  // open: clk, Q, Qn, preset, en, reset
  D_Flip_Flop d_ff_12 ();  // open: clk, D, Q, Qn, preset, en, reset
  D_Flip_Flop d_ff_13 (.D(in_1[6]));  // open: clk, Q, Qn, preset, en, reset
  D_Flip_Flop d_ff_14 ();  // open: clk, D, Q, Qn, preset, en, reset
  D_Flip_Flop d_ff_15 (.D(in_1[7]));  // open: clk, Q, Qn, preset, en, reset
  D_Flip_Flop d_ff_16 ();  // open: clk, D, Q, Qn, preset, en, reset
endmodule
