// Logisim project register.circ as structural Verilog: 2 circuits, main circuit singleRegister
module singleRegister (
  input  Reset,
  input  [15:0] In,
  output [15:0] Out
);

  wire clock_1_out, x1;

  Clock clock_1 (.out(clock_1_out));
  D_Flip_Flop d_ff_1 (.clk(clock_1_out), .D(In[0]), .Q(Out[0]), .reset(Reset));  // open: Qn, preset, en
  D_Flip_Flop d_ff_2 (.clk(clock_1_out), .D(In[1]), .Q(x1), .reset(Reset));  // open: Qn, preset, en
  D_Flip_Flop d_ff_3 (.clk(clock_1_out), .D(In[2]), .Q(Out[2]), .reset(Reset));  // open: Qn, preset, en
  D_Flip_Flop d_ff_4 (.clk(clock_1_out), .D(In[3]), .Q(Out[3]));  // open: Qn, preset, en, reset
  D_Flip_Flop d_ff_5 (.clk(clock_1_out), .D(In[4]), .Q(Out[4]), .reset(Reset));  // open: Qn, preset, en
  D_Flip_Flop d_ff_6 (.clk(clock_1_out), .D(In[5]), .Q(Out[5]), .reset(Reset));  // open: Qn, preset, en
  D_Flip_Flop d_ff_7 (.clk(clock_1_out), .D(In[6]), .Q(Out[6]), .reset(Reset));  // open: Qn, preset, en
  D_Flip_Flop d_ff_8 (.clk(clock_1_out), .D(In[7]), .Q(Out[7]));  // open: Qn, preset, en, reset
  D_Flip_Flop d_ff_9 (.clk(clock_1_out), .D(In[8]), .Q(Out[8]), .reset(Reset));  // open: Qn, preset, en
  D_Flip_Flop d_ff_10 (.clk(clock_1_out), .D(In[9]), .Q(Out[9]), .reset(Reset));  // open: Qn, preset, en
  D_Flip_Flop d_ff_11 (.clk(clock_1_out), .D(In[10]), .Q(Out[10]), .reset(Reset));  // open: Qn, preset, en
  D_Flip_Flop d_ff_12 (.clk(clock_1_out), .D(In[11]), .Q(Out[11]));  // open: Qn, preset, en, reset
  D_Flip_Flop d_ff_13 (.clk(clock_1_out), .D(In[12]), .Q(Out[12]), .reset(Reset));  // open: Qn, preset, en
  D_Flip_Flop d_ff_14 (.clk(clock_1_out), .D(In[13]), .Q(Out[13]), .reset(Reset));  // open: Qn, preset, en
  D_Flip_Flop d_ff_15 (.clk(clock_1_out), .D(In[14]), .Q(Out[14]), .reset(Reset));  // open: Qn, preset, en
  D_Flip_Flop d_ff_16 (.clk(clock_1_out), .D(In[15]), .Q(Out[15]));  // open: Qn, preset, en, reset

  assign Out[1] = Out[2];

  // Other names for the same wires on the sheet: _0 = In[0]; _1 = In[1]; _2 = In[2]; _3 = In[3]; _4 = In[4];
  //   _5 = In[5]; _6 = In[6]; _7 = In[7]; _8 = In[8]; _9 = In[9]; _10 = In[10]; _11 = In[11]; _12 = In[12];
  //   _13 = In[13]; _14 = In[14]; _15 = In[15]; x0 = Out[0]; x2 = Out[2]; x3 = Out[3]; x4 = Out[4]; x5 = Out[5];
  //   x6 = Out[6]; x7 = Out[7]; x8 = Out[8]; x9 = Out[9]; x10 = Out[10]; x11 = Out[11]; x12 = Out[12]; x13 = Out[13];
  //   x14 = Out[14]; x15 = Out[15]
endmodule

module registerFile (
  input  in_1
);

  singleRegister singleregister_1 (.Reset(in_1));  // open: Out, In
  singleRegister singleregister_2 (.Reset(in_1));  // open: Out, In
  singleRegister singleregister_3 (.Reset(in_1));  // open: Out, In
  singleRegister singleregister_4 (.Reset(in_1));  // open: Out, In
endmodule
