// Logisim project adder.circ as structural Verilog: 2 circuits, main circuit actualMain
module main (
  input  A,
  input  B,
  input  carryIn,
  output Sum,
  output carryOut
);

  wire and_1_out, and_2_out, and_3_out, and_4_out, and_5_out, and_6_out, and_7_out, not_1_out, not_2_out,
       not_3_out;

  not not_1 (not_1_out, A);
  not not_2 (not_2_out, B);
  not not_3 (not_3_out, carryIn);
  and and_1 (and_1_out, not_1_out, not_2_out, carryIn);
  and and_2 (and_2_out, not_1_out, B, not_3_out);
  and and_3 (and_3_out, A, not_2_out, not_3_out);
  and and_4 (and_4_out, A, B, carryIn);
  and and_5 (and_5_out, B, carryIn);
  and and_6 (and_6_out, B, A);
  and and_7 (and_7_out, carryIn, A);
  or or_1 (Sum, and_1_out, and_2_out, and_3_out, and_4_out);
  or or_2 (carryOut, and_5_out, and_6_out, and_7_out);
endmodule

module actualMain (
  input  carryIn,
  input  A0,
  input  B0,
  input  A1,
  input  B1,
  input  A2,
  input  B2,
  input  A3,
  input  B3,
  input  A4,
  input  B4,
  input  A5,
  input  B5,
  input  A6,
  input  B6,
  input  A7,
  input  B7,
  input  A8,
  input  B8,
  input  A9,
  input  B9,
  input  A10,
  input  B10,
  input  A11,
  input  B11,
  input  A12,
  input  B12,
  input  A13,
  input  B13,
  input  A14,
  input  B14,
  input  A15,
  input  B15,
  output Sum0,
  output Sum1,
  output Sum2,
  output Sum3,
  output Sum4,
  output Sum5,
  output Sum6,
  output Sum7,
  output Sum8,
  output Sum9,
  output Sum10,
  output Sum11,
  output Sum12,
  output Sum13,
  output Sum14,
  output Sum15,
  output carryOut
);

  wire main_1_carryout, main_2_carryout, main_3_carryout, main_4_carryout, main_5_carryout, main_6_carryout,
       main_7_carryout, main_9_carryout, main_10_carryout, main_11_carryout, main_12_carryout,
       main_13_carryout, main_14_carryout, main_15_carryout;

  main main_1 (.A(A0), .B(B0), .carryIn(carryIn), .Sum(Sum0), .carryOut(main_1_carryout));
  main main_2 (.A(A1), .B(B1), .carryIn(main_1_carryout), .Sum(Sum1), .carryOut(main_2_carryout));
  main main_3 (.A(A2), .B(B2), .carryIn(main_2_carryout), .Sum(Sum2), .carryOut(main_3_carryout));
  main main_4 (.A(A3), .B(B3), .carryIn(main_3_carryout), .Sum(Sum3), .carryOut(main_4_carryout));
  main main_5 (.A(A4), .B(A4), .carryIn(main_4_carryout), .Sum(Sum4), .carryOut(main_5_carryout));
  main main_6 (.A(A5), .B(B5), .carryIn(main_5_carryout), .Sum(Sum5), .carryOut(main_6_carryout));
  main main_7 (.A(A6), .B(B6), .carryIn(main_6_carryout), .Sum(Sum6), .carryOut(main_7_carryout));
  main main_8 (.A(A7), .B(B7), .carryIn(main_7_carryout), .Sum(Sum7), .carryOut(B8));
  main main_9 (.A(A8), .B(B8), .carryIn(B8), .Sum(Sum8), .carryOut(main_9_carryout));
  main main_10 (.A(A9), .B(B9), .carryIn(main_9_carryout), .Sum(Sum9), .carryOut(main_10_carryout));
  main main_11 (.A(A10), .B(B10), .carryIn(main_10_carryout), .Sum(Sum10), .carryOut(main_11_carryout));
  main main_12 (.A(A11), .B(B11), .carryIn(main_11_carryout), .Sum(Sum11), .carryOut(main_12_carryout));
  main main_13 (.A(A12), .B(A12), .carryIn(main_12_carryout), .Sum(Sum12), .carryOut(main_13_carryout));
  main main_14 (.A(A13), .B(B13), .carryIn(main_13_carryout), .Sum(Sum13), .carryOut(main_14_carryout));
  main main_15 (.A(A14), .B(B14), .carryIn(main_14_carryout), .Sum(Sum14), .carryOut(main_15_carryout));
  main main_16 (.A(A15), .B(B15), .carryIn(main_15_carryout), .Sum(Sum15), .carryOut(carryOut));

  assign B4 = A4;
  assign B12 = A12;
endmodule
