// Logisim project question6.circ as structural Verilog: 1 circuit, main circuit main
module main (
  input  in1,
  input  in2,
  output \output 
);

  wire and_1_out, and_2_out, and_3_out, and_4_out, clock_1_out, clock_2_out, D0_Q0_q, D0_Q0_qn, D1_Q1_q,
       not_1_out, not_2_out, or_1_out, or_2_out, or_3_out;

  not not_1 (not_1_out, in1);
  not not_2 (not_2_out, in2);
  and and_1 (and_1_out, in1, not_2_out);
  and and_2 (and_2_out, not_1_out, in2);
  or or_1 (or_1_out, and_1_out, and_2_out);
  Clock clock_1 (.out(clock_1_out));
  and and_3 (and_3_out, or_1_out, or_2_out);
  or or_2 (or_2_out, D1_Q1_q, D0_Q0_q);
  Clock clock_2 (.out(clock_2_out));
  or or_3 (or_3_out, D1_Q1_q, D0_Q0_qn);
  and and_4 (and_4_out, or_3_out, or_1_out);
  D_Flip_Flop D1_Q1 (.clk(clock_1_out), .D(and_3_out), .Q(D1_Q1_q));  // open: Qn, preset, en, reset
  D_Flip_Flop D0_Q0 (.clk(clock_2_out), .D(and_4_out), .Q(D0_Q0_q), .Qn(D0_Q0_qn));  // open: preset, en, reset
  and and_5 (\output , D1_Q1_q, D0_Q0_q);
endmodule
